// Logisim project RELAYS.circ as structural Verilog: 5 circuits, main circuit DPDT
module Main (
);

  DPDT dpdt_1 ();  // open: coil, NC, com, NO, NC_2, com_2, NO_2
  DPDTr dpdtr_1 ();  // open: coil, com, com_2, NC, NO, NC_2, NO_2
endmodule

module DPDT (
  input  coil,
  input  NC,
  input  NO,
  input  NC_2,
  input  NO_2,
  output com,
  output com_2
);

  Pull_Resistor pull_resistor_1 (.node(coil));
  Multiplexer #(.enable("false")) multiplexer_1 (.in0(NC), .in1(NO), .out(com), .sel(coil));
  Multiplexer #(.enable("false")) multiplexer_2 (.in0(NC_2), .in1(NO_2), .out(com_2), .sel(coil));
endmodule

module DPDTr (
  input  coil,
  input  com,
  input  com_2,
  output NC,
  output NO,
  output NC_2,
  output NO_2
);

  Demultiplexer #(.tristate("true")) demultiplexer_1 (.out0(NC), .out1(NO), .in(com), .sel(coil));  // open: en
  Demultiplexer #(.tristate("true")) demultiplexer_2 (.out0(NC_2), .out1(NO_2), .in(com_2), .sel(coil));  // open: en
  Pull_Resistor pull_resistor_1 (.node(coil));
endmodule

module SPDT (
  input  coil,
  input  NC,
  input  NO,
  output com
);

  Pull_Resistor pull_resistor_1 (.node(coil));
  Multiplexer #(.enable("false")) multiplexer_1 (.in0(NC), .in1(NO), .out(com), .sel(coil));
endmodule

module DPDTb (
  input  coil,
  input  com,
  input  NC,
  input  NO,
  output NC_2,
  output NO_2,
  output com_2
);

  Demultiplexer #(.tristate("true")) demultiplexer_1 (.out0(NC_2), .out1(NO_2), .in(com), .sel(coil));  // open: en
  Pull_Resistor pull_resistor_1 (.node(coil));
  Multiplexer #(.enable("false")) multiplexer_1 (.in0(NC), .in1(NO), .out(com_2), .sel(coil));
endmodule
